// Logisim project 1. laboratorijska vaja.circ as structural Verilog: 1 circuit, main circuit main
module main (
  input  x1,
  input  x2,
  input  x3,
  input  x4,
  output f_x1__x2__x3__x4
);

  wire and_1_out, not_1_out, xor_1_out;

  and and_1 (and_1_out, x1, x2);
  not not_1 (not_1_out, and_1_out);
  xor xor_1 (xor_1_out, x2, x4);
  or or_1 (f_x1__x2__x3__x4, not_1_out, x3, xor_1_out);
endmodule
