// Logisim project 10. laboratorijska naloga.circ as structural Verilog: 2 circuits, main circuit main
module main (
  input  x,
  output y1,
  output y2
);

  wire clock_1_out, t12_1_t1, t12_1_t2, t_ff_1_q, t_ff_1_qn, t_ff_2_q, t_ff_2_qn;

  t12 t12_1 (.q1(t_ff_1_q), .q2(t_ff_2_q), .x(x), .t1(t12_1_t1), .t2(t12_1_t2));
  Clock clock_1 (.out(clock_1_out));
  T_Flip_Flop t_ff_1 (.clk(clock_1_out), .T(t12_1_t1), .Q(t_ff_1_q), .Qn(t_ff_1_qn));  // open: preset, reset, en
  T_Flip_Flop t_ff_2 (.clk(clock_1_out), .T(t12_1_t2), .Q(t_ff_2_q), .Qn(t_ff_2_qn));  // open: preset, reset, en
  and and_1 (y1, t_ff_1_q, t_ff_2_qn);
  and and_2 (y2, t_ff_1_qn, t_ff_2_q);
endmodule

module t12 (
  input  q1,
  input  q2,
  input  x,
  output t1,
  output t2
);

  wire and_1_out, and_2_out, and_3_out, and_4_out, and_5_out, and_6_out, not_1_out, not_2_out, not_3_out;

  not not_1 (not_1_out, q1);
  not not_2 (not_2_out, q2);
  not not_3 (not_3_out, x);
  and and_1 (and_1_out, q1, q2);
  and and_2 (and_2_out, not_1_out, not_2_out);
  and and_3 (and_3_out, q1, not_3_out);
  and and_4 (and_4_out, not_2_out, x);
  and and_5 (and_5_out, q2, not_3_out);
  and and_6 (and_6_out, q1, not_3_out);
  or or_1 (t1, and_1_out, and_2_out, and_3_out);
  or or_2 (t2, and_4_out, and_5_out, and_6_out);
endmodule
