// Logisim project 2. laboratorijska vaja.circ as structural Verilog: 1 circuit, main circuit main
module main (
  input  x1,
  input  x,
  input  x3,
  input  x4,
  output out_5
);

  wire not_1_out, not_2_out, not_3_out, not_4_out, or_1_out, or_2_out, or_3_out, or_4_out, or_5_out,
       or_6_out, or_7_out, or_8_out;

  not not_1 (not_1_out, x1);
  not not_2 (not_2_out, x);
  not not_3 (not_3_out, x3);
  not not_4 (not_4_out, x4);
  or or_1 (or_1_out, x1, x, x3, not_4_out);
  or or_2 (or_2_out, x1, x, not_3_out, x4);
  or or_3 (or_3_out, x1, not_2_out, x3, not_4_out);
  or or_4 (or_4_out, x1, not_2_out, not_3_out, x4);
  and and_1 (out_5, or_1_out, or_2_out, or_3_out, or_4_out, or_5_out, or_7_out, or_6_out, or_8_out);
  or or_5 (or_5_out, not_1_out, x, x3, not_4_out);
  or or_6 (or_6_out, not_1_out, not_2_out, x3, not_4_out);
  or or_7 (or_7_out, not_1_out, x, not_3_out, x4);
  or or_8 (or_8_out, not_1_out, not_2_out, not_3_out, x4);
endmodule
