// Logisim project 7. domača naloga.circ as structural Verilog: 1 circuit, main circuit main
module main (
  input  I0,
  input  I1,
  input  x,
  output y
);

  wire and_1_out, and_2_out, not_1_out;

  not not_1 (not_1_out, x);
  and and_1 (and_1_out, I0, x);
  and and_2 (and_2_out, I1, not_1_out);
  or or_1 (y, and_1_out, and_2_out);
endmodule
