// Logisim project 7. laboratorijska naloga.circ as structural Verilog: 1 circuit, main circuit main
module main (
  input  x1,
  input  x2,
  input  x3,
  input  x4,
  output out_5
);

  wire multiplexer_1_out, not_1_out;

  not not_1 (not_1_out, x4);
  Multiplexer #(.select(2)) multiplexer_1 (
    .in0(x4), .in1(x4), .in2(not_1_out), .in3(x4), .out(multiplexer_1_out), .sel({x1, x3}));  // open: en
  Multiplexer multiplexer_2 (.in0(1'b1), .in1(multiplexer_1_out), .out(out_5), .sel(x2));  // open: en
endmodule
