// Logisim project 7. laboratorijska vaja.circ as structural Verilog: 1 circuit, main circuit main
module main (
  input  x1,
  input  x2,
  input  x3,
  output f
);

  wire not_1_out, not_2_out, not_3_out;

  not not_1 (not_1_out, x1);
  not not_2 (not_2_out, x2);
  not not_3 (not_3_out, x3);
  Multiplexer #(.select(2)) multiplexer_1 (
    .in0(not_3_out), .in1(not_3_out), .in2(x3), .in3(1'b1), .out(f), .sel({x1, x2}));  // open: en
endmodule
