// Logisim project 7.1. laboratorijska vaja.circ as structural Verilog: 1 circuit, main circuit main
module main (
  input  x1,
  input  x2,
  input  x3,
  output out_4
);

  wire not_1_out;

  not not_1 (not_1_out, x3);
  Multiplexer #(.select(2)) multiplexer_1 (
    .in0(1'b0), .in1(not_1_out), .in2(not_1_out), .in3(not_1_out), .out(out_4), .sel({x1, x2}));  // open: en
endmodule
