// Logisim project 7.b domača naloga.circ as structural Verilog: 1 circuit, main circuit main
module main (
  input  x1,
  input  x2,
  input  x3,
  input  x4,
  output y
);

  wire multiplexer_1_out, multiplexer_2_out, multiplexer_3_out, multiplexer_4_out;

  Multiplexer multiplexer_1 (.in0(1'b1), .in1(1'b0), .out(multiplexer_1_out), .sel(x4));  // open: en
  Multiplexer multiplexer_2 (.in0(1'b1), .in1(1'b0), .out(multiplexer_2_out), .sel(x2));  // open: en
  Multiplexer multiplexer_3 (.in0(multiplexer_1_out), .in1(x4), .out(multiplexer_3_out), .sel(x2));  // open: en
  Multiplexer multiplexer_4 (
    .in0(multiplexer_2_out), .in1(multiplexer_3_out), .out(multiplexer_4_out), .sel(x1));  // open: en
  Multiplexer multiplexer_5 (.in0(multiplexer_4_out), .in1(1'b1), .out(y), .sel(x3));  // open: en
endmodule
