// Logisim project 8. laboratorijska naloga.circ as structural Verilog: 3 circuits, main circuit main
module main (
  input  in_1,
  input  in_2,
  output out_3
);

  wire clock_1_out, not_1_out, not_2_out, r_1_out_4, s_1_out_4;

  Clock clock_1 (.out(clock_1_out));
  not not_1 (not_1_out, in_1);
  not not_2 (not_2_out, in_2);
  s s_1 (.x(in_1), .y(in_2), .z(out_3), .out_4(s_1_out_4));
  r r_1 (.x(in_1), .y(in_2), .z(out_3), .out_4(r_1_out_4));
  S_R_Flip_Flop s_r_ff_1 (.S(s_1_out_4), .clk(clock_1_out), .R(r_1_out_4), .Q(out_3));  // open: Qn, preset, reset, en
endmodule

module r (
  input  x,
  input  y,
  input  z,
  output out_4
);

  wire and_1_out, and_2_out, not_1_out, not_2_out, not_3_out;

  not not_1 (not_1_out, x);
  not not_2 (not_2_out, y);
  not not_3 (not_3_out, z);
  and and_1 (and_1_out, x, y, z);
  and and_2 (and_2_out, not_1_out, not_2_out, z);
  or or_1 (out_4, and_1_out, and_2_out);
endmodule

module s (
  input  x,
  input  y,
  input  z,
  output out_4
);

  wire and_1_out, and_2_out, not_1_out, not_2_out, not_3_out;

  not not_1 (not_1_out, x);
  not not_2 (not_2_out, y);
  not not_3 (not_3_out, z);
  and and_1 (and_1_out, not_1_out, not_3_out);
  and and_2 (and_2_out, y, not_3_out);
  or or_1 (out_4, and_1_out, and_2_out);
endmodule
