// Logisim project 8. laboratorijska vaja.circ as structural Verilog: 2 circuits, main circuit main
module main (
  input  x,
  input  y,
  output q
);

  wire clock_1_out, k_1_k, not_1_out, not_2_out;

  Clock clock_1 (.out(clock_1_out));
  not not_1 (not_1_out, x);
  not not_2 (not_2_out, y);
  k k_1 (.x(x), .y(y), .k(k_1_k));
  J_K_Flip_Flop j_k_ff_1 (.J(not_2_out), .clk(clock_1_out), .K(k_1_k), .Q(q));  // open: Qn, preset, en, reset
endmodule

module k (
  input  x,
  input  y,
  output k
);

  wire and_1_out, and_2_out, not_1_out, not_2_out;

  not not_1 (not_1_out, x);
  not not_2 (not_2_out, y);
  and and_1 (and_1_out, not_1_out, y);
  and and_2 (and_2_out, x, not_2_out);
  or or_1 (k, and_1_out, and_2_out);
endmodule
