// Logisim project 9. domača naloga.circ as structural Verilog: 3 circuits, main circuit main
module main (
  input  x1,
  input  x2,
  input  x3,
  output q
);

  wire clock_1_out, j_1_j, k_1_k, not_1_out, not_2_out, not_3_out;

  not not_1 (not_1_out, x1);
  not not_2 (not_2_out, x2);
  not not_3 (not_3_out, x3);
  k k_1 (.x1(x1), .x2(x2), .x3(x3), .k(k_1_k));
  Clock clock_1 (.out(clock_1_out));
  j j_1 (.x1(x1), .x2(x2), .x3(x3), .j(j_1_j));
  J_K_Flip_Flop j_k_ff_1 (.J(j_1_j), .clk(clock_1_out), .K(k_1_k), .Q(q));  // open: Qn, preset, en, reset
endmodule

module k (
  input  x1,
  input  x2,
  input  x3,
  output k
);

  wire and_1_out, and_2_out, and_3_out, not_1_out, not_2_out;

  not not_1 (not_1_out, x1);
  not not_2 (not_2_out, x3);
  and and_1 (and_1_out, not_1_out, x2);
  and and_2 (and_2_out, x2, not_2_out);
  and and_3 (and_3_out, not_1_out, not_2_out);
  or or_1 (k, and_1_out, and_2_out, and_3_out);
endmodule

module j (
  input  x1,
  input  x2,
  input  x3,
  output j
);

  wire and_1_out, and_2_out, and_3_out;

  and and_1 (and_1_out, x1, x2);
  and and_2 (and_2_out, x2, x3);
  and and_3 (and_3_out, x1, x3);
  or or_1 (j, and_1_out, and_2_out, and_3_out);
endmodule
