// Logisim project Dodatna domača naloga.circ as structural Verilog: 1 circuit, main circuit main
module main (
  input  x1,
  input  x2,
  input  x3,
  output f
);

  wire and_1_out, not_1_out, not_2_out, not_3_out, or_1_out;

  not not_1 (not_1_out, x1);
  not not_2 (not_2_out, x2);
  not not_3 (not_3_out, x3);
  and and_1 (and_1_out, not_1_out, not_2_out);
  or or_1 (or_1_out, x3, and_1_out);
  not not_4 (f, or_1_out);
endmodule
